# Fritzing sketch servo motor (saved by Fritzing 0.9.4)

parts:
  SERVO1 = Tower Pro SG90 servo [part_number=101246]
  Part1 = Arduino Uno (Rev3)

nets:
  N1: SERVO1.Signal, Part1.D9_PWM
  +5V: SERVO1.+5V, Part1.5V
  GND: SERVO1.GND, Part1.GND

custom parts:
  Tower Pro SG90 servo: Original file by John De Cristofaro http://www.adafruit.com/products/1449 Adafruit Feedback Servo (Small) Edited by: e-radionica.com 28/9/2015
